# Fritzing sketch 2022 11.19.1 Stepper Motor Controller (saved by Fritzing 0.9.9b)
circuit board: 9.93339cm x 8cm

parts:
  J2 = Reed Relay [part_number=CTB0158-4 package=THT]
  Switch1 = female pin header, 2 pins [form="♀ (female)"]
  Switch3 = female pin header, 2 pins [form="♀ (female)"]
  Part2 = Buck Converter [package="SIP (Single Inline) [THT]"]
  U2 = SIP - 6 pins [chip_label="M.D. Cur Sens" package="SIP (Single Inline) [THT]"]  # not connected
  Pololu_A1 = Pololu A4988 [package=SO16]
  LED1 = LED - 5mm [color="Red (633nm)" current=0.030 package="5 mm [THT]"]
  Switch7 = female pin header, 2 pins [form="♀ (female)"]
  Switch8 = female pin header, 2 pins [form="♀ (female)"]
  M1 = Stepper Motor - Bipolar
  R3 = Resistor [tolerance=±5% power=0.25 resistance=220 package=THT]
  S2 = Taiway 100-SP-X-T1 SPDT Miniature Toggle Switch [part_number=100-SP-X-T1-0-0-B1-M1 package=THT]  # not connected
  Switch2 = female pin header, 2 pins [form="♀ (female)"]
  M2 = DOIT Esp32 DevKit v1 (30 pins long, 11 pins width) [part_number=ESP32S-PIN30]
  Switch10 = female pin header, 3 pins [form="♀ (female)"]
  Fuse1 = Fuse with Handler [part_number=Htc-15m]
  R5 = Resistor [tolerance=±5% power=0.25 resistance=220 package=THT]
  Switch5 = female pin header, 2 pins [form="♀ (female)"]  # not connected
  JP4 = Header 5x2 [package=avr_icsp]
  J9 = female pin header, 4 pins [form="♀ (female)"]
  Version_D7 = Amazon 2596 Buck Converter
  LED2 = LEDs [package=led-1206]
  J6 = female pin header, 4 pins [form="♀ (female)"]

nets:
  N1: J2.pin1, J9.pin3
  GND: J2.pin2, Part2.GND, Pololu_A1.GND#14, Switch2.pin1, M2.GND, Switch10.pin1, JP4.1, JP4.3, JP4.5, JP4.7, JP4.9, J9.pin1, Version_D7.Pin_2, Version_D7.Pin_4
  N2: J2.pin3, M2.D15
  N3: J2.pin4, J9.pin4
  N4: Switch1.pin1, Switch3.pin1
  N5: Switch1.pin2, R3.Pin_1
  N6: Switch3.pin2, R5.Pin_0
  12V: Part2.Vcc, Pololu_A1.VMOT, Version_D7.Pin_3
  N7: Part2.Vout, M2.VIN
  N8: Pololu_A1.ENABLE, M2.D25
  N9: Pololu_A1.RESET, Pololu_A1.SLEEP
  N10: Pololu_A1.STEP, M2.D33
  N11: Pololu_A1.DIR, M2.D32
  3.3V: Pololu_A1.VDD, J6.pin3
  N12: Pololu_A1.1B, Pololu_A1.1A, M1.A, M1.C
  N13: Pololu_A1.2A, M1.B
  N14: Pololu_A1.2B, M1.D
  N15: LED1.cathode, Switch7.pin1
  N16: LED1.anode, Switch7.pin2
  N17: Switch8.pin1, LED2.A
  N18: Switch8.pin2, LED2.C
  N19: R3.Pin_0, M2.D27
  N20: Switch2.pin2, M2.D26
  N21: M2.3V3, Switch10.pin2, J6.pin4
  N22: M2.D2, JP4.2
  N23: M2.D4, JP4.4
  N24: M2.RX2, JP4.6
  N25: M2.TX2, JP4.8
  N26: M2.D5, JP4.10
  N27: M2.D21, J6.pin2
  N28: M2.D22, J6.pin1
  N29: M2.VP, Switch10.pin3
  N30: M2.D14, R5.Pin_1
  N31: Fuse1.Connector1, J9.pin2
  N32: Fuse1.Connector2, Version_D7.Pin_1

notes:
  Green
  Red
  Switch
  Reed Relay
  220
  100
  11/09/2022  SDFWA Member Shop
  11/19/2022  SDFWA Member Shop
  4"
  5"
  30
  60
  120
  Delay

custom parts:
  Reed Relay: SIL Reed Relay 0.2" pitch
  Buck Converter: Amazon Buck Converter Output Voltage is user settable
  SIP - 6 pins: Modern Devices Current sensor
  DOIT Esp32 DevKit v1 (30 pins long, 11 pins width): The DOIT Esp32 DevKit v1 is one of the development board created by DOIT to evaluate the ESP-WROOM-32 module. It is based on the ESP32 microcontroller that boasts Wifi, Bluetooth, Ethernet and Low Power support all in a single chip. (vanepp) made breadboard work, adjusted pin numbering and labels and reduced size of schematic and cleaned up pcb. This chip is 30pins long (2 x15) and 11 pins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
